# Fritzing sketch arduinoledmatrixproximity (saved by Fritzing 0.9.3b)
breadboards: 1

parts:
  Part1 = Arduino Uno (Rev3)
  R1 = PHOTOCELL [package=photocell]
  R2 = Resistor [tolerance=±5% resistance=1k package=THT]
  Part2 = Adafruit CharliePlex Driver IS31FL3731 [part_number="Adafruit #2946"]
  Part3 = LED Charlieplexed Matrix - 9x16 [part_number=2947]  # not connected

nets:
  N1: Part1.A0, R1.P$1, R2.Pin_1
  N2: Part1.A4/SDA, Part2.SDA
  N3: Part1.A5/SCL, Part2.SCL
  N4: Part1.3V3, R1.P$2
  5V: Part1.5V, Part2.VCC
  GND: Part1.GND, R2.Pin_0, Part2.GND

custom parts:
  Adafruit CharliePlex Driver IS31FL3731: The IS31FL3731 will let you get back to that classic LED matrix look, with a nice upgrade! This I2C LED driver chip has the ability to PWM each individual LED in a 16x9 grid so you can have beautiful LED lighting effects, without a lot of pin twiddling. Simply tell the chip which LED on the grid you want lit, and what brightness and it's all taken care of for you. The IS31FL3731 is a nice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
  LED Charlieplexed Matrix - 9x16: The IS31FL3731 will let you get back to that classic LED matrix look, with a nice upgrade! This I2C LED driver chip has the ability to PWM each individual LED in a 16x9 grid so you can have beautiful LED lighting effects, without a lot of pin twiddling. Simply tell the chip which LED on the grid you want lit, and what brightness and it's all taken care of for you.
